// Logisim project lab06part1.circ as structural Verilog: 1 circuit, main circuit main
module main (
  input  A,
  input  B,
  input  C,
  output S,
  output C_out
);

  wire A1_out, A2_out, A3_out, A4_out, A5_out, A6_out, A7_out, A8_out, A9_out, A10_out, A11_out, not_1_out,
       not_2_out, not_3_out, O1_out, O2_out, O4_out;

  not not_1 (not_1_out, A);
  not not_2 (not_2_out, B);
  not not_3 (not_3_out, C);
  and A5 (A5_out, A, not_2_out);
  and A7 (A7_out, A, B);
  and A9 (A9_out, C, A);
  and A10 (A10_out, C, B);
  and A11 (A11_out, B, A);
  and A1 (A1_out, not_1_out, not_2_out);
  and A3 (A3_out, not_1_out, B);
  and A4 (A4_out, A3_out, not_3_out);
  or O4 (O4_out, A9_out, A10_out);
  and A2 (A2_out, A1_out, C);
  and A6 (A6_out, A5_out, not_3_out);
  and A8 (A8_out, A7_out, C);
  or O5 (C_out, O4_out, A11_out);
  or O1 (O1_out, A2_out, A4_out);
  or O2 (O2_out, A6_out, A8_out);
  or O3 (S, O1_out, O2_out);
endmodule
