// Logisim project lab06part2.circ as structural Verilog: 1 circuit, main circuit main
module main (
  input  in_1,
  input  [7:0] A,
  input  [7:0] B,
  input  in_4,
  output [7:0] out_5
);

  wire [7:0] adder_1_out, subtractor_1_out;

  // Probe on adder_1_out
  Adder adder_1 (.a(A), .b(B), .out(adder_1_out), .cin(in_1));  // open: cout
  // Probe on subtractor_1_out
  Subtractor subtractor_1 (.a(A), .b(B), .out(subtractor_1_out), .bin(in_1));  // open: bout
  Multiplexer #(.width(8)) multiplexer_1 (
    .in0(adder_1_out), .in1(subtractor_1_out), .out(out_5), .sel(in_4));  // open: en
endmodule
