// Logisim project lab06part2.circ as structural Verilog: 1 circuit, main circuit main
module main (
  input  in_1,
  input  [7:0] in_2,
  input  [7:0] in_3,
  input  in_4,
  output [7:0] out_5
);

  wire [7:0] adder_1_out, subtractor_1_out;

  Adder adder_1 (.a(in_2), .b(in_3), .out(adder_1_out), .cin(in_1));  // open: cout
  Subtractor subtractor_1 (.a(in_2), .b(in_3), .out(subtractor_1_out), .bin(in_1));  // open: bout
  // Probe on adder_1_out
  // Probe on subtractor_1_out
  Multiplexer #(.width(8), .disabled("Z")) multiplexer_1 (
    .in0(adder_1_out), .in1(subtractor_1_out), .out(out_5), .sel(in_4));  // open: en

  // Notes on the sheet:
  //   A
  //   B
  //   Adder Probe
  //   Subtractor Probe
endmodule
