// Logisim project 1bit_ALU.circ as structural Verilog: 3 circuits, main circuit main
module main (
  input  [3:0] ALU_Operation,
  input  [7:0] in_2,
  input  [7:0] in_3,
  output Zero,
  output out_5,
  output out_6,
  output out_7,
  output out_8,
  output out_9,
  output out_10,
  output out_11,
  output out_12,
  output out_13,
  output out_14,
  output Overflow
);

  wire bitselector_1_out;
  wire [1:1] undriven;

  BitSelector #(.width(2)) bitselector_1 (
    .in({undriven[1], ALU_Operation[1]}), .out(bitselector_1_out), .sel(ALU_Operation[0]));
  // EightBitALU eightbitalu_1: pin names not known; wires that end beside it: in_3[2], bitselector_1_out, in_2[0], in_3[0], in_2[1], in_3[1], in_2[2], in_2[3], in_3[3], in_2[4], in_3[4], in_2[5], in_3[5], in_2[6], in_3[6], in_2[7], in_3[7], ALU_Operation[2], Overflow, ALU_Operation[3], out_14, out_13, Zero, out_12, out_11, out_10, out_9, out_8, out_7, out_6, out_5
  // Pins of 1 and 2 bits meet at {undriven[1], ALU_Operation[1]}

  // Notes on the sheet:
  //   A
  //   B
  //   Result
endmodule

module ALU (
  input  Ainvert,
  input  [1:0] Operation,
  input  Binvert,
  input  CarryIn,
  input  A,
  input  B,
  input  Less,
  output Result,
  output CarryOut,
  output Set
);

  wire and_1_out, multiplexer_1_out, multiplexer_2_out, not_1_out, not_2_out, or_1_out;

  Multiplexer #(.enable("false")) multiplexer_1 (.in0(A), .in1(not_1_out), .out(multiplexer_1_out), .sel(Ainvert));
  not not_1 (not_1_out, A);
  Multiplexer #(.enable("false")) multiplexer_2 (.in0(B), .in1(not_2_out), .out(multiplexer_2_out), .sel(Binvert));
  not not_2 (not_2_out, B);
  and and_1 (and_1_out, multiplexer_1_out, multiplexer_2_out);
  or or_1 (or_1_out, multiplexer_1_out, multiplexer_2_out);
  Adder #(.width(1)) adder_1 (.a(multiplexer_1_out), .b(multiplexer_2_out), .out(Set), .cin(CarryIn), .cout(CarryOut));
  Multiplexer #(.select(2), .enable("false")) multiplexer_3 (
    .in0(and_1_out), .in1(or_1_out), .in2(Set), .in3(Less), .out(Result), .sel(Operation));
endmodule

module EightBitALU (
  input  Ainvert,
  input  Bnegate,
  input  [1:0] Operation,
  input  a0,
  input  b0,
  input  a1,
  input  b1,
  input  _0,
  input  a1_2,
  input  b1_2,
  input  _0_2,
  input  a1_3,
  input  b1_3,
  input  _0_3,
  input  a1_4,
  input  b1_4,
  input  _0_4,
  input  a1_5,
  input  b1_5,
  input  _0_5,
  input  a1_6,
  input  b1_6,
  input  _0_6,
  input  a1_7,
  input  b1_7,
  input  _0_7,
  output out_27,
  output out_28,
  output Zero,
  output out_30,
  output out_31,
  output out_32,
  output Result,
  output out_34,
  output out_35,
  output out_36,
  output Overflow
);

  wire alu_1_carryout, alu_2_carryout, alu_3_carryout, alu_4_carryout, alu_5_carryout, alu_6_carryout,
       alu_7_carryout, alu_8_set, or_1_out;

  ALU alu_1 (
    .A(a0), .B(b0), .Less(alu_8_set), .Ainvert(Ainvert), .Binvert(Bnegate), .CarryIn(Bnegate),
    .Operation(Operation), .CarryOut(alu_1_carryout), .Result(out_27));  // open: Set
  ALU alu_2 (
    .A(a1), .B(b1), .Less(_0), .Ainvert(Ainvert), .Binvert(Bnegate), .CarryIn(alu_1_carryout),
    .Operation(Operation), .CarryOut(alu_2_carryout), .Result(out_28));  // open: Set
  ALU alu_3 (
    .A(a1_2), .B(b1_2), .Less(_0_2), .Ainvert(Ainvert), .Binvert(Bnegate), .CarryIn(alu_2_carryout),
    .Operation(Operation), .CarryOut(alu_3_carryout), .Result(out_30));  // open: Set
  ALU alu_4 (
    .A(a1_3), .B(b1_3), .Less(_0_3), .Ainvert(Ainvert), .Binvert(Bnegate), .CarryIn(alu_3_carryout),
    .Operation(Operation), .CarryOut(alu_4_carryout), .Result(out_31), .Set(out_31));
  ALU alu_5 (
    .A(a1_4), .B(b1_4), .Less(_0_4), .Ainvert(Ainvert), .Binvert(Bnegate), .CarryIn(alu_4_carryout),
    .Operation(Operation), .CarryOut(alu_5_carryout), .Result(out_32));  // open: Set
  ALU alu_6 (
    .A(a1_5), .B(b1_5), .Less(_0_5), .Ainvert(Ainvert), .Binvert(Bnegate), .CarryIn(alu_5_carryout),
    .Operation(Operation), .CarryOut(alu_6_carryout), .Result(out_34));  // open: Set
  ALU alu_7 (
    .A(a1_6), .B(b1_6), .Less(_0_6), .Ainvert(Ainvert), .Binvert(Bnegate), .CarryIn(alu_6_carryout),
    .Operation(Operation), .CarryOut(alu_7_carryout), .Result(out_35));  // open: Set
  ALU alu_8 (
    .A(a1_7), .B(b1_7), .Less(_0_7), .Ainvert(Ainvert), .Binvert(Bnegate), .CarryIn(alu_7_carryout),
    .Operation(Operation), .CarryOut(Overflow), .Result(out_36), .Set(alu_8_set));
  or or_1 (or_1_out, out_27, out_28, out_30, out_36);
  not not_1 (Zero, or_1_out);
  or or_2 (Result, out_31, out_32, out_34, out_35);

  // Notes on the sheet:
  //   Result0
  //   Result1
  //   Result2
  //   Result3
  //   Result4
  //   Result5
  //   Result6
  //   Result7
  //   Set
endmodule
