// Logisim project lab08.circ as structural Verilog: 3 circuits, main circuit main
module main (
  input  [3:0] ALU_Operation,
  input  [7:0] in_2,
  input  [7:0] in_3,
  output Zero,
  output [7:0] out_5,
  output Overflow
);

  EightBitALU eightbitalu_1 (
    .Operation(ALU_Operation), .in_2(in_2), .B(in_3), .Zero(Zero), .out_5(out_5), .Overflow(Overflow));

  // Notes on the sheet:
  //   A
  //   B
  //   Result
endmodule

module ALU (
  input  Ainvert,
  input  [1:0] Operation,
  input  Binvert,
  input  CarryIn,
  input  A,
  input  B,
  input  Less,
  output Result,
  output CarryOut,
  output Set
);

  wire and_1_out, multiplexer_1_out, multiplexer_2_out, not_1_out, not_2_out, or_1_out;

  Multiplexer #(.enable("false")) multiplexer_1 (.in0(A), .in1(not_1_out), .out(multiplexer_1_out), .sel(Ainvert));
  not not_1 (not_1_out, A);
  Multiplexer #(.enable("false")) multiplexer_2 (.in0(B), .in1(not_2_out), .out(multiplexer_2_out), .sel(Binvert));
  not not_2 (not_2_out, B);
  and and_1 (and_1_out, multiplexer_1_out, multiplexer_2_out);
  or or_1 (or_1_out, multiplexer_1_out, multiplexer_2_out);
  Adder #(.width(1)) adder_1 (.a(multiplexer_1_out), .b(multiplexer_2_out), .out(Set), .cin(CarryIn), .cout(CarryOut));
  Multiplexer #(.select(2), .enable("false")) multiplexer_3 (
    .in0(and_1_out), .in1(Set), .in2(or_1_out), .in3(Less), .out(Result), .sel(Operation));
endmodule

module EightBitALU (
  input  [3:0] Operation,
  input  [7:0] in_2,
  input  [7:0] B,
  output Zero,
  output [7:0] out_5,
  output Overflow
);

  wire alu_1_carryout, alu_2_carryout, alu_3_carryout, alu_4_carryout, alu_5_carryout, alu_6_carryout,
       alu_7_carryout, alu_8_set, or_1_out;

  ALU alu_1 (
    .A(in_2[0]), .B(B[0]), .Less(alu_8_set), .Ainvert(Operation[3]), .Binvert(Operation[2]),
    .CarryIn(Operation[2]), .Operation(Operation[1:0]), .CarryOut(alu_1_carryout), .Result(out_5[0]));  // open: Set
  ALU alu_2 (
    .A(in_2[1]), .B(B[1]), .Ainvert(Operation[3]), .Binvert(Operation[2]), .CarryIn(alu_1_carryout),
    .Operation(Operation[1:0]), .CarryOut(alu_2_carryout), .Result(out_5[1]));  // open: Less, Set
  ALU alu_3 (
    .A(in_2[2]), .B(B[2]), .Ainvert(Operation[3]), .Binvert(Operation[2]), .CarryIn(alu_2_carryout),
    .Operation(Operation[1:0]), .CarryOut(alu_3_carryout), .Result(out_5[2]));  // open: Less, Set
  ALU alu_4 (
    .A(B[3]), .B(in_2[3]), .Ainvert(Operation[3]), .Binvert(Operation[2]), .CarryIn(alu_3_carryout),
    .Operation(Operation[1:0]), .CarryOut(alu_4_carryout), .Result(out_5[3]), .Set(out_5[3]));  // open: Less
  ALU alu_5 (
    .A(B[4]), .B(in_2[4]), .Ainvert(Operation[3]), .Binvert(Operation[2]), .CarryIn(alu_4_carryout),
    .Operation(Operation[1:0]), .CarryOut(alu_5_carryout), .Result(out_5[4]));  // open: Less, Set
  ALU alu_6 (
    .A(B[5]), .B(in_2[5]), .Ainvert(Operation[3]), .Binvert(Operation[2]), .CarryIn(alu_5_carryout),
    .Operation(Operation[1:0]), .CarryOut(alu_6_carryout), .Result(out_5[5]));  // open: Less, Set
  ALU alu_7 (
    .A(in_2[6]), .B(B[6]), .Ainvert(Operation[3]), .Binvert(Operation[2]), .CarryIn(alu_6_carryout),
    .Operation(Operation[1:0]), .CarryOut(alu_7_carryout), .Result(out_5[6]));  // open: Less, Set
  ALU alu_8 (
    .A(in_2[7]), .B(B[7]), .Ainvert(Operation[3]), .Binvert(Operation[2]), .CarryIn(alu_7_carryout),
    .Operation(Operation[1:0]), .CarryOut(Overflow), .Result(out_5[7]), .Set(alu_8_set));  // open: Less
  or or_1 (or_1_out, out_5[0], out_5[1], out_5[2], out_5[3], out_5[4], out_5[5], out_5[6], out_5[7]);
  not not_1 (Zero, or_1_out);

  // Notes on the sheet:
  //   A
  //   Ainvert
  //   Bnegate
  //   a0
  //   b0
  //   a1
  //   b1
  //   a2
  //   b2
  //   a3
  //   b3
  //   a4
  //   b4
  //   a5
  //   b5
  //   a6
  //   b6
  //   a7
  //   b7
  //   Result0
  //   Result1
  //   Result2
  //   Result3
  //   Result4
  //   Result5
  //   Result6
  //   Result7
  //   Set
  //   Result
endmodule
