// Logisim project lab09_adp59.circ as structural Verilog: 1 circuit, main circuit main
module main (
  input  [2:0] readRegister1,
  input  [2:0] readRegister2,
  input  writeEnable,
  input  [2:0] writeRegister,
  input  [31:0] writeData,
  input  in_6,
  output [31:0] readData1,
  output [31:0] readData2
);

  wire decoder_1_out0, decoder_1_out1, decoder_1_out2, decoder_1_out3, decoder_1_out4, decoder_1_out5,
       decoder_1_out6, decoder_1_out7, undriven, undriven_2, undriven_3;
  wire [31:0] Reg0_q, Reg1_q, Reg2_q, Reg3_q, Reg4_q, Reg5_q, Reg6_q, Reg7_q;

  Decoder #(.select(3)) decoder_1 (
    .out0(decoder_1_out0), .out1(decoder_1_out1), .out2(decoder_1_out2), .out3(decoder_1_out3),
    .out4(decoder_1_out4), .out5(decoder_1_out5), .out6(decoder_1_out6), .out7(decoder_1_out7),
    .sel(writeRegister), .en(writeEnable));
  Register #(.width(32)) Reg0 (.D(writeData), .en(decoder_1_out0), .clk(in_6), .Q(Reg0_q));  // open: clr
  Register #(.width(32)) Reg1 (.D(writeData), .en(decoder_1_out1), .clk(in_6), .Q(Reg1_q), .clr(undriven));
  Register #(.width(32)) Reg2 (.D(writeData), .en(decoder_1_out2), .clk(in_6), .Q(Reg2_q), .clr(undriven_2));
  Register #(.width(32)) Reg3 (.D(writeData), .en(decoder_1_out3), .clk(in_6), .Q(Reg3_q), .clr(undriven_3));
  Register #(.width(32)) Reg4 (.D(writeData), .en(decoder_1_out4), .clk(in_6), .Q(Reg4_q));  // open: clr
  Register #(.width(32)) Reg5 (.D(writeData), .en(decoder_1_out5), .clk(in_6), .Q(Reg5_q));  // open: clr
  Register #(.width(32)) Reg6 (.D(writeData), .en(decoder_1_out6), .clk(in_6), .Q(Reg6_q));  // open: clr
  Register #(.width(32)) Reg7 (.D(writeData), .en(decoder_1_out7), .clk(in_6), .Q(Reg7_q));  // open: clr
  Multiplexer #(.select(3), .width(32), .enable("false")) multiplexer_1 (
    .in0(Reg0_q), .in1(Reg1_q), .in2(Reg2_q), .in3(Reg3_q), .in4(Reg4_q), .in5(Reg5_q), .in6(Reg6_q),
    .in7(Reg7_q), .out(readData1), .sel(readRegister1));
  Multiplexer #(.select(3), .width(32), .enable("false")) multiplexer_2 (
    .in0(Reg0_q), .in1(Reg1_q), .in2(Reg2_q), .in3(Reg3_q), .in4(Reg4_q), .in5(Reg5_q), .in6(Reg6_q),
    .in7(Reg7_q), .out(readData2), .sel(readRegister2));
endmodule
