// Logisim project lab09_firstDraft.circ as structural Verilog: 1 circuit, main circuit main
module main (
  input  writeEnable,
  input  [2:0] readRegister1,
  input  [1:0] in_3,
  input  [2:0] readRegister2,
  input  [1:0] in_5,
  input  [2:0] writeRegister,
  input  [1:0] in_7,
  input  [31:0] writeData,
  input  in_9,
  output [31:0] readData1,
  output [31:0] readData2
);

  Demultiplexer #(.width(5), .enable("false")) demultiplexer_1 ();  // open: out0, out1, in, sel
  Decoder decoder_1 ();  // open: out0, out1, sel, en
  Register #(.width(32)) Reg0 (.clr(in_9));  // open: D, en, clk, Q
  Register #(.width(32)) Reg1 (.clr(in_9));  // open: D, en, clk, Q
  Register #(.width(32)) Reg0_2 (.clr(in_9));  // open: D, en, clk, Q
  Register #(.width(32)) Reg1_2 (.clr(in_9));  // open: D, en, clk, Q
endmodule
