// Logisim project lab09_secondDraft.circ as structural Verilog: 1 circuit, main circuit main
module main (
  input  writeEnable,
  input  [31:0] writeData,
  input  [2:0] readRegister1,
  input  [1:0] in_4,
  input  [2:0] readRegister2,
  input  [1:0] in_6,
  input  [2:0] writeRegister,
  input  [1:0] in_8,
  input  in_9,
  input  [15:0] \input ,
  input  [3:0] write_register_2f234c09,
  input  [3:0] read_register_0_43f3239c,
  input  single_reg_instr_da00fc8e,
  input  [3:0] read_register_1_219819a4,
  input  write,
  output [31:0] readData1,
  output [31:0] readData2,
  output [15:0] output_0_892e24c9,
  output [15:0] output_1_93275966
);

  wire and_2_out, and_3_out, and_4_out, and_5_out, and_6_out, and_7_out, and_8_out, and_9_out, and_10_out,
       and_11_out, and_12_out, and_13_out, and_14_out, and_15_out, and_16_out, not_1_out, not_2_out,
       not_3_out, not_4_out, not_5_out, not_6_out, not_7_out, not_8_out, not_9_out, not_10_out, not_11_out,
       not_12_out, not_13_out, not_14_out, not_15_out, not_16_out, not_17_out, not_18_out, not_19_out,
       not_20_out, not_21_out, not_22_out, not_23_out, not_24_out, not_25_out, not_26_out, not_27_out,
       not_28_out, not_29_out, not_30_out, not_31_out, not_32_out;
  wire [2:0] demultiplexer_1_out0, demultiplexer_1_out1, demultiplexer_1_out2, demultiplexer_1_out3,
       demultiplexer_2_out0, demultiplexer_2_out1, demultiplexer_2_out2, demultiplexer_2_out3,
       demultiplexer_3_out0, demultiplexer_3_out1, demultiplexer_3_out2, demultiplexer_3_out3;
  wire [3:0] multiplexer_4_out;
  wire [15:0] register_6_q, register_7_q, register_8_q, register_9_q, register_10_q, register_11_q,
       register_12_q, register_13_q, register_14_q, register_15_q, register_16_q;

  Demultiplexer #(.select(2), .width(3), .enable("false")) demultiplexer_1 (
    .out0(demultiplexer_1_out0), .out1(demultiplexer_1_out1), .out2(demultiplexer_1_out2),
    .out3(demultiplexer_1_out3), .in(readRegister1), .sel(in_4));
  Demultiplexer #(.select(2), .width(3), .enable("false")) demultiplexer_2 (
    .out0(demultiplexer_2_out0), .out1(demultiplexer_2_out1), .out2(demultiplexer_2_out2),
    .out3(demultiplexer_2_out3), .in(readRegister2), .sel(in_6));
  Demultiplexer #(.select(2), .width(3), .enable("false")) demultiplexer_3 (
    .out0(demultiplexer_3_out0), .out1(demultiplexer_3_out1), .out2(demultiplexer_3_out2),
    .out3(demultiplexer_3_out3), .in(writeRegister), .sel(in_8));
  not not_1 (not_1_out, write_register_2f234c09[0]);
  not not_2 (not_2_out, write_register_2f234c09[1]);
  not not_3 (not_3_out, write_register_2f234c09[2]);
  not not_4 (not_4_out, write_register_2f234c09[3]);
  not not_5 (not_5_out, write_register_2f234c09[1]);
  not not_6 (not_6_out, write_register_2f234c09[2]);
  not not_7 (not_7_out, write_register_2f234c09[3]);
  not not_8 (not_8_out, write_register_2f234c09[0]);
  not not_9 (not_9_out, write_register_2f234c09[2]);
  not not_10 (not_10_out, write_register_2f234c09[3]);
  not not_11 (not_11_out, write_register_2f234c09[2]);
  not not_12 (not_12_out, write_register_2f234c09[3]);
  not not_13 (not_13_out, write_register_2f234c09[0]);
  not not_14 (not_14_out, write_register_2f234c09[1]);
  not not_15 (not_15_out, write_register_2f234c09[3]);
  not not_16 (not_16_out, write_register_2f234c09[1]);
  not not_17 (not_17_out, write_register_2f234c09[3]);
  not not_18 (not_18_out, write_register_2f234c09[0]);
  not not_19 (not_19_out, write_register_2f234c09[3]);
  not not_20 (not_20_out, write_register_2f234c09[3]);
  not not_21 (not_21_out, write_register_2f234c09[0]);
  not not_22 (not_22_out, write_register_2f234c09[1]);
  not not_23 (not_23_out, write_register_2f234c09[2]);
  not not_24 (not_24_out, write_register_2f234c09[1]);
  not not_25 (not_25_out, write_register_2f234c09[2]);
  not not_26 (not_26_out, write_register_2f234c09[0]);
  not not_27 (not_27_out, write_register_2f234c09[2]);
  not not_28 (not_28_out, write_register_2f234c09[2]);
  not not_29 (not_29_out, write_register_2f234c09[0]);
  not not_30 (not_30_out, write_register_2f234c09[1]);
  not not_31 (not_31_out, write_register_2f234c09[1]);
  not not_32 (not_32_out, write_register_2f234c09[0]);
  Register #(.width(32)) Reg0 (.D(writeData), .en(writeEnable), .clr(in_9));  // open: clk, Q
  Register #(.width(32)) Reg1 (.D(writeData), .en(writeEnable), .clr(in_9));  // open: clk, Q
  Register #(.width(32)) Reg2 (.D(writeData), .en(writeEnable), .clr(in_9));  // open: clk, Q
  Register #(.width(32)) Reg3 (.D(writeData), .en(writeEnable), .clr(in_9));  // open: clk, Q
  Register #(.width(32)) Reg4 (.D(writeData), .en(writeEnable), .clr(in_9));  // open: clk, Q
  Register #(.width(32)) Reg5 (.D(writeData), .en(writeEnable), .clr(in_9));  // open: clk, Q
  Register #(.width(32)) Reg6 (.D(writeData), .en(writeEnable), .clr(in_9));  // open: clk, Q
  Register #(.width(32)) Reg7 (.D(writeData), .en(writeEnable), .clr(in_9));  // open: clk, Q
  and and_1 (\input [0], not_2_out, not_4_out);
  and and_2 (and_2_out, not_5_out, not_7_out);
  and and_3 (and_3_out, write_register_2f234c09[1], not_10_out);
  and and_4 (and_4_out, write_register_2f234c09[1], not_12_out);
  and and_5 (and_5_out, not_14_out, not_15_out);
  and and_6 (and_6_out, not_16_out, not_17_out);
  and and_7 (and_7_out, write_register_2f234c09[1], not_19_out);
  and and_8 (and_8_out, write_register_2f234c09[1], not_20_out);
  and and_9 (and_9_out, not_22_out, write_register_2f234c09[3]);
  and and_10 (and_10_out, not_24_out, write_register_2f234c09[3]);
  and and_11 (and_11_out, write_register_2f234c09[1], write_register_2f234c09[3]);
  and and_12 (and_12_out, write_register_2f234c09[1], write_register_2f234c09[3]);
  and and_13 (and_13_out, not_30_out, write_register_2f234c09[3]);
  and and_14 (and_14_out, not_31_out, write_register_2f234c09[3]);
  and and_15 (and_15_out, write_register_2f234c09[1], write_register_2f234c09[3]);
  and and_16 (and_16_out, write_register_2f234c09[1], write_register_2f234c09[3]);
  Register #(.width(16)) register_1 (.D(\input ), .en(\input [0]), .clk(\input [0]));  // open: Q, clr
  // Register #(.width(16)) register_2: pin names not known; wires that end beside it: and_2_out, and_3_out
  // Register #(.width(16)) register_3: pin names not known; wires that end beside it: and_3_out, and_4_out
  // Register #(.width(16)) register_4: pin names not known; wires that end beside it: and_4_out, and_5_out, \input 
  Register #(.width(16)) register_5 ();  // open: D, en, clk, Q, clr
  Register #(.width(16)) register_6 (.D(\input ), .Q(register_6_q), .clk(and_6_out));  // open: en, clr
  Register #(.width(16)) register_7 (.D(\input ), .Q(register_7_q), .clk(and_7_out));  // open: en, clr
  Register #(.width(16)) register_8 (.D(\input ), .Q(register_8_q), .clk(and_8_out));  // open: en, clr
  Register #(.width(16)) register_9 (.D(\input ), .Q(register_9_q), .clk(and_9_out));  // open: en, clr
  Register #(.width(16)) register_10 (.D(\input ), .Q(register_10_q), .clk(and_10_out));  // open: en, clr
  Register #(.width(16)) register_11 (.D(\input ), .Q(register_11_q), .clk(and_11_out));  // open: en, clr
  Register #(.width(16)) register_12 (.D(\input ), .Q(register_12_q), .clk(and_12_out));  // open: en, clr
  Register #(.width(16)) register_13 (.D(\input ), .Q(register_13_q), .clk(and_13_out));  // open: en, clr
  Register #(.width(16)) register_14 (.D(\input ), .Q(register_14_q), .clk(and_14_out));  // open: en, clr
  Register #(.width(16)) register_15 (.D(\input ), .Q(register_15_q), .clk(and_15_out));  // open: en, clr
  Register #(.width(16)) register_16 (.D(\input ), .Q(register_16_q), .clk(and_16_out));  // open: en, clr
  Multiplexer #(.select(5), .width(32), .enable("false")) multiplexer_1 (.out(readData1));  // open: in0, in1, in2, in3, in4, in5, in6, in7, in8, in9, in10, in11, in12, in13, in14, in15, in16, in17, in18, in19, in20, in21, in22, in23, in24, in25, in26, in27, in28, in29, in30, in31, sel
  Multiplexer #(.select(5), .width(32), .enable("false")) multiplexer_2 (.out(readData2));  // open: in0, in1, in2, in3, in4, in5, in6, in7, in8, in9, in10, in11, in12, in13, in14, in15, in16, in17, in18, in19, in20, in21, in22, in23, in24, in25, in26, in27, in28, in29, in30, in31, sel
  Multiplexer #(.select(4), .width(16), .enable("false")) multiplexer_3 (
    .in0(\input ), .in1(\input ), .in2(\input ), .in3(\input ), .in4(\input ), .in5(register_6_q),
    .in6(register_7_q), .in7(register_8_q), .in8(register_9_q), .in9(register_10_q), .in10(register_11_q),
    .in11(register_12_q), .in12(register_13_q), .in13(register_14_q), .in14(register_15_q),
    .in15(register_16_q), .out(output_0_892e24c9), .sel(multiplexer_4_out));
  Multiplexer #(.width(4), .enable("false")) multiplexer_4 (
    .in0(read_register_0_43f3239c), .in1(write_register_2f234c09), .out(multiplexer_4_out),
    .sel(single_reg_instr_da00fc8e));
  Multiplexer #(.select(4), .width(16), .enable("false")) multiplexer_5 (
    .in0(\input ), .in1(\input ), .in2(\input ), .in3(\input ), .in4(\input ), .in5(register_6_q),
    .in6(register_7_q), .in7(register_8_q), .in8(register_9_q), .in9(register_10_q), .in10(register_11_q),
    .in11(register_12_q), .in12(register_13_q), .in13(register_14_q), .in14(register_15_q),
    .in15(register_16_q), .out(output_1_93275966), .sel(read_register_1_219819a4));
  // Pins of 1 and 16 bits meet at \input 

  // Other names for the same wires on the sheet: wr[3:0] = write_register_2f234c09
endmodule
