// Logisim project lab10.circ as structural Verilog: 4 circuits, main circuit main
module main (
);

  wire and_1_out, and_2_out, Clock_out, control_1_dstmux, fields_1_register, not_1_out;
  wire [1:0] control_1_alu;
  wire [3:0] fields_1_opcode;
  wire [7:0] A_q, adder_1_out, alu_1_output, B_q, Counter_q, fields_1_immediate, multiplexer_1_out;
  wire [15:0] ROM_data;

  Clock Clock (.out(Clock_out));
  Adder adder_1 (.a(Counter_q), .b(8'h1), .out(adder_1_out));  // open: cin, cout
  Register Counter (.D(adder_1_out), .en(1'b1), .clk(Clock_out), .Q(Counter_q));  // open: clr
  ROM #(.dataWidth(16)) ROM (.addr(Counter_q), .data(ROM_data));
  Fields fields_1 (
    .Input8bits(ROM_data), .Immediate(fields_1_immediate), .Register(fields_1_register),
    .OpCode(fields_1_opcode));
  Control control_1 (.Input4Bits(fields_1_opcode), .ALU(control_1_alu), .DstMux(control_1_dstmux));
  and and_1 (and_1_out, fields_1_register, 1'b1);
  not not_1 (not_1_out, and_2_out);
  and and_2 (and_2_out, fields_1_register, 1'b1);
  Register B (.D(multiplexer_1_out), .en(and_1_out), .clk(Clock_out), .Q(B_q));  // open: clr
  Register A (.D(multiplexer_1_out), .en(not_1_out), .clk(Clock_out), .Q(A_q));  // open: clr
  ALU alu_1 (.B(B_q), .A(A_q), .Operation(control_1_alu), .\output (alu_1_output));
  Multiplexer #(.width(8), .enable("false")) multiplexer_1 (
    .in0(alu_1_output), .in1(fields_1_immediate), .out(multiplexer_1_out), .sel(control_1_dstmux));

  // Notes on the sheet:
  //   Fetch
  //   contents of ROM (hex, n*v repeats v):
  //   1 802
  //   SetMux
endmodule

module Fields (
  input  [15:0] Input8bits,
  output [7:0] Immediate,
  output Register,
  output [3:0] OpCode
);


  assign Immediate = Input8bits[7:0];
  assign OpCode = Input8bits[15:12];
  assign Register = Input8bits[11];
endmodule

module Control (
  input  [3:0] Input4Bits,
  output [1:0] ALU,
  output DstMux
);

  wire not_2_out, not_3_out;

  not not_1 (ALU[1], Input4Bits[1]);
  not not_2 (not_2_out, Input4Bits[2]);
  not not_3 (not_3_out, Input4Bits[1]);
  and and_1 (DstMux, not_2_out, not_3_out);

  assign ALU[0] = Input4Bits[0];
endmodule

module ALU (
  input  [1:0] Operation,
  input  [7:0] B,
  input  [7:0] A,
  output [7:0] \output 
);

  wire [7:0] adder_1_out, and_1_out, or_1_out, subtractor_1_out;

  Adder adder_1 (.a(B), .b(A), .out(adder_1_out));  // open: cin, cout
  Subtractor subtractor_1 (.a(B), .b(A), .out(subtractor_1_out));  // open: bin, bout
  assign and_1_out = B & A;  // AND_Gate and_1, 8 bits wide
  assign or_1_out = B | A;  // OR_Gate or_1, 8 bits wide
  Multiplexer #(.select(2), .width(8), .enable("false")) multiplexer_1 (
    .in0(adder_1_out), .in1(subtractor_1_out), .in2(and_1_out), .in3(or_1_out), .out(\output ),
    .sel(Operation));
endmodule
