// Logisim project lab10.circ as structural Verilog: 6 circuits, main circuit main
module main (
);

  wire and_1_out, and_2_out, Clock_out, control_1_dstmux, fields_1_register, not_1_out;
  wire [1:0] control_1_alu;
  wire [3:0] fields_1_opcode;
  wire [7:0] A_q, adder_1_out, aluv2_1_output, B_q, Counter_q, fields_1_immediate, multiplexer_1_out;
  wire [15:0] ROM_data;

  Clock Clock (.out(Clock_out));
  Adder adder_1 (.a(Counter_q), .b(8'h1), .out(adder_1_out));  // open: cin, cout
  Register Counter (.D(adder_1_out), .en(1'b1), .clk(Clock_out), .Q(Counter_q));  // open: clr
  ROM #(.dataWidth(16)) ROM (.addr(Counter_q), .data(ROM_data));
  Fields fields_1 (
    .Input8bits(ROM_data), .Immediate(fields_1_immediate), .Register(fields_1_register),
    .OpCode(fields_1_opcode));
  Control control_1 (.Input4Bits(fields_1_opcode), .ALU(control_1_alu), .DstMux(control_1_dstmux));
  and and_1 (and_1_out, fields_1_register, 1'b1);
  not not_1 (not_1_out, and_2_out);
  and and_2 (and_2_out, fields_1_register, 1'b1);
  Register B (.D(multiplexer_1_out), .en(and_1_out), .clk(Clock_out), .Q(B_q));  // open: clr
  Register A (.D(multiplexer_1_out), .en(not_1_out), .clk(Clock_out), .Q(A_q));  // open: clr
  ALUv2 aluv2_1 (.B(B_q), .A(A_q), .Operation(control_1_alu), .\output (aluv2_1_output));
  Multiplexer #(.width(8), .enable("false")) multiplexer_1 (
    .in0(aluv2_1_output), .in1(fields_1_immediate), .out(multiplexer_1_out), .sel(control_1_dstmux));

  // Notes on the sheet:
  //   Fetch
  //   contents of ROM (hex, n*v repeats v):
  //   1 802
  //   SetMux
endmodule

module ALU (
  input  Ainvert,
  input  [1:0] Operation,
  input  Binvert,
  input  CarryIn,
  input  A,
  input  B,
  input  Less,
  output Result,
  output CarryOut,
  output Set
);

  wire and_1_out, multiplexer_1_out, multiplexer_2_out, not_1_out, not_2_out, or_1_out;

  Multiplexer #(.enable("false")) multiplexer_1 (.in0(A), .in1(not_1_out), .out(multiplexer_1_out), .sel(Ainvert));
  not not_1 (not_1_out, A);
  Multiplexer #(.enable("false")) multiplexer_2 (.in0(B), .in1(not_2_out), .out(multiplexer_2_out), .sel(Binvert));
  not not_2 (not_2_out, B);
  and and_1 (and_1_out, multiplexer_1_out, multiplexer_2_out);
  or or_1 (or_1_out, multiplexer_1_out, multiplexer_2_out);
  Adder #(.width(1)) adder_1 (.a(multiplexer_1_out), .b(multiplexer_2_out), .out(Set), .cin(CarryIn), .cout(CarryOut));
  Multiplexer #(.select(2), .enable("false")) multiplexer_3 (
    .in0(and_1_out), .in1(Set), .in2(or_1_out), .in3(Less), .out(Result), .sel(Operation));
endmodule

module eightBitALU (
  input  [3:0] Operation,
  input  [7:0] in_2,
  input  [7:0] B,
  output Zero,
  output [7:0] out_5,
  output Overflow
);

  wire alu_1_carryout, alu_2_carryout, alu_3_carryout, alu_4_carryout, alu_5_carryout, alu_6_carryout,
       alu_7_carryout, alu_8_set, or_1_out;

  ALU alu_1 (
    .A(in_2[0]), .B(B[0]), .Less(alu_8_set), .Ainvert(Operation[3]), .Binvert(Operation[2]),
    .CarryIn(Operation[2]), .Operation(Operation[1:0]), .CarryOut(alu_1_carryout), .Result(out_5[0]));  // open: Set
  ALU alu_2 (
    .A(in_2[1]), .B(B[1]), .Ainvert(Operation[3]), .Binvert(Operation[2]), .CarryIn(alu_1_carryout),
    .Operation(Operation[1:0]), .CarryOut(alu_2_carryout), .Result(out_5[1]));  // open: Less, Set
  ALU alu_3 (
    .A(in_2[2]), .B(B[2]), .Ainvert(Operation[3]), .Binvert(Operation[2]), .CarryIn(alu_2_carryout),
    .Operation(Operation[1:0]), .CarryOut(alu_3_carryout), .Result(out_5[2]));  // open: Less, Set
  ALU alu_4 (
    .A(B[3]), .B(in_2[3]), .Ainvert(Operation[3]), .Binvert(Operation[2]), .CarryIn(alu_3_carryout),
    .Operation(Operation[1:0]), .CarryOut(alu_4_carryout), .Result(out_5[3]), .Set(out_5[3]));  // open: Less
  ALU alu_5 (
    .A(B[4]), .B(in_2[4]), .Ainvert(Operation[3]), .Binvert(Operation[2]), .CarryIn(alu_4_carryout),
    .Operation(Operation[1:0]), .CarryOut(alu_5_carryout), .Result(out_5[4]));  // open: Less, Set
  ALU alu_6 (
    .A(B[5]), .B(in_2[5]), .Ainvert(Operation[3]), .Binvert(Operation[2]), .CarryIn(alu_5_carryout),
    .Operation(Operation[1:0]), .CarryOut(alu_6_carryout), .Result(out_5[5]));  // open: Less, Set
  ALU alu_7 (
    .A(in_2[6]), .B(B[6]), .Ainvert(Operation[3]), .Binvert(Operation[2]), .CarryIn(alu_6_carryout),
    .Operation(Operation[1:0]), .CarryOut(alu_7_carryout), .Result(out_5[6]));  // open: Less, Set
  ALU alu_8 (
    .A(in_2[7]), .B(B[7]), .Ainvert(Operation[3]), .Binvert(Operation[2]), .CarryIn(alu_7_carryout),
    .Operation(Operation[1:0]), .CarryOut(Overflow), .Result(out_5[7]), .Set(alu_8_set));  // open: Less
  or or_1 (or_1_out, out_5[0], out_5[1], out_5[2], out_5[3], out_5[4], out_5[5], out_5[6], out_5[7]);
  not not_1 (Zero, or_1_out);

  // Notes on the sheet:
  //   A
  //   Ainvert
  //   Bnegate
  //   a0
  //   b0
  //   a1
  //   b1
  //   a2
  //   b2
  //   a3
  //   b3
  //   a4
  //   b4
  //   a5
  //   b5
  //   a6
  //   b6
  //   a7
  //   b7
  //   Result0
  //   Result1
  //   Result2
  //   Result3
  //   Result4
  //   Result5
  //   Result6
  //   Result7
  //   Set
  //   Result
endmodule

module Fields (
  input  [15:0] Input8bits,
  output [7:0] Immediate,
  output Register,
  output [3:0] OpCode
);


  assign Immediate = Input8bits[7:0];
  assign OpCode = Input8bits[15:12];
  assign Register = Input8bits[11];
endmodule

module Control (
  input  [3:0] Input4Bits,
  output [1:0] ALU,
  output DstMux
);

  wire not_2_out, not_3_out;

  not not_1 (ALU[1], Input4Bits[1]);
  not not_2 (not_2_out, Input4Bits[2]);
  not not_3 (not_3_out, Input4Bits[1]);
  and and_1 (DstMux, not_2_out, not_3_out);

  assign ALU[0] = Input4Bits[0];
endmodule

// ALU
module ALUv2 (
  input  [1:0] Operation,
  input  [7:0] B,
  input  [7:0] A,
  output [7:0] \output 
);

  wire [7:0] adder_1_out, and_1_out, or_1_out, subtractor_1_out;

  Adder adder_1 (.a(B), .b(A), .out(adder_1_out));  // open: cin, cout
  Subtractor subtractor_1 (.a(B), .b(A), .out(subtractor_1_out));  // open: bin, bout
  assign and_1_out = B & A;  // AND_Gate and_1, 8 bits wide
  assign or_1_out = B | A;  // OR_Gate or_1, 8 bits wide
  Multiplexer #(.select(2), .width(8), .enable("false")) multiplexer_1 (
    .in0(adder_1_out), .in1(subtractor_1_out), .in2(and_1_out), .in3(or_1_out), .out(\output ),
    .sel(Operation));
endmodule
